// Digital circuit 1-ALU.dig as structural Verilog
module _1_ALU (
  input  [7:0] A,
  input  [7:0] B,
  input  c_i,
  input  [2:0] M_Con,
  output Car,
  output Over,
  output [7:0] Out
);

  wire if_sum_1_out, over_1_flag, SR_A_Cout, SR_B_Cout, SUM_Cout;
  wire [7:0] AND, OR, SR_A, SR_B, SUM, XOR;

  // SUM sum_1: pin names not known; wires that end beside it: c_i, A, B, SUM_Cout, SUM
  AND and_1 (.A(A), .B(B), .Out(AND));
  OR or_1 (.A(A), .B(B), .Out(OR));
  XOR xor_1 (.A(A), .B(B), .Out(XOR));
  SR sr_1 (.In(A), .Out(SR_A), .Cout(SR_A_Cout));
  SR sr_2 (.In(B), .Out(SR_B), .Cout(SR_B_Cout));
  OVER over_1 (.Overflow(SUM[7]), .A(A), .B(B), .FLAG(over_1_flag));
  IF_SUM if_sum_1 (.In(M_Con), .Out(if_sum_1_out));
  and and_2 (Over, if_sum_1_out, over_1_flag);
  Multiplexer #(.Selector_Bits(3)) multiplexer_1 (
    .sel(M_Con), .in_0(SUM_Cout), .in_1(1'b0), .in_2(1'b0), .in_3(1'b0), .in_4(SR_A_Cout), .in_5(SR_B_Cout),
    .in_6(1'b0), .in_7(1'b0), .out(Car));
  Multiplexer #(.Selector_Bits(3), .Bits(8)) multiplexer_2 (
    .sel(M_Con), .in_0(SUM), .in_1(AND), .in_2(OR), .in_3(XOR), .in_4(SR_A), .in_5(SR_B), .in_6(A), .in_7(B),
    .out(Out));

  // Other names for the same wires on the sheet: CTRL[2:0] = M_Con
endmodule
