// Digital circuit 2-BUS.dig as structural Verilog
module _2_BUS (
  input  [30:0] Ctrl,
  input  [7:0] DB_in,
  input  Clock,
  input  IR5,
  input  C_in,
  input  [3:0] Ctrl_P,
  input  [7:0] ADL_in,
  output [7:0] SP_out,
  output [7:0] SB_out,
  output [7:0] ADD_out,
  output [7:0] Out
);

  wire ACR, AVR, not_1_out, or_1_out, or_2_out;
  wire [7:0] _1_alu_1_out, A_q, ACC_q, ADD_q, B_q, DB, driver_10_out, X_q, Y_q;

  _3_P _3_p_1 (.IR5(IR5), .DB_in(DB), .DB_out(DB), .Ctrl({Ctrl_P, Ctrl[30:20]}), .ACR(ACR), .AVR(AVR), .Clock(Clock));
  or or_1 (or_1_out, Ctrl[2], Ctrl[4], Ctrl[14]);
  not not_1 (not_1_out, or_1_out);
  assign DB = not_1_out ? DB_in : 8'bz;  // Driver driver_1
  Register #(.Bits(8)) u_OUT (.D(DB), .C(Clock), .en(Ctrl[19]), .Q(Out));
  assign DB = Ctrl[2] ? ACC_q : 8'bz;  // Driver driver_2
  Register #(.Bits(8)) ACC (.D(DB), .C(Clock), .en(Ctrl[1]), .Q(ACC_q));
  assign DB = Ctrl[4] ? SP_out : 8'bz;  // Driver driver_3
  Register #(.Bits(8)) SP (.D(DB), .C(Clock), .en(Ctrl[13]), .Q(SP_out));
  assign DB = Ctrl[14] ? SB_out : 8'bz;  // Driver driver_4
  assign SB_out = Ctrl[15] ? DB : 8'bz;  // Driver driver_5
  assign SB_out = Ctrl[0] ? ACC_q : 8'bz;  // Driver driver_6
  assign SB_out = Ctrl[3] ? SP_out : 8'bz;  // Driver driver_7
  assign SB_out = Ctrl[6] ? X_q : 8'bz;  // Driver driver_8
  assign SB_out = Ctrl[8] ? Y_q : 8'bz;  // Driver driver_9
  Register #(.Bits(8)) X (.D(SB_out), .C(Clock), .en(Ctrl[5]), .Q(X_q));
  Register #(.Bits(8)) Y (.D(SB_out), .C(Clock), .en(Ctrl[7]), .Q(Y_q));
  assign driver_10_out = Ctrl[11] ? SB_out : 8'bz;  // Driver driver_10
  assign driver_10_out = Ctrl[12] ? ADL_in : 8'bz;  // Driver driver_11
  _1_ALU _1_alu_1 (.A(A_q), .B(B_q), .c_i(C_in), .M_Con(Ctrl[18:16]), .Car(ACR), .Over(AVR), .Out(_1_alu_1_out));
  Register #(.Bits(8)) B (.D(driver_10_out), .C(Clock), .en(or_2_out), .Q(B_q));
  PullDown #(.Bits(8)) pulldown_1 (.out(driver_10_out));
  or or_2 (or_2_out, Ctrl[11], Ctrl[12]);
  Register #(.Bits(8)) ADD (.D(_1_alu_1_out), .C(Clock), .en(1'b1), .Q(ADD_q));
  Register #(.Bits(8)) A (.D(DB), .C(Clock), .en(Ctrl[10]), .Q(A_q));
  assign ADD_out = Ctrl[9] ? ADD_q : 8'bz;  // Driver driver_12
  PullDown #(.Bits(8)) pulldown_2 (.out(ADD_out));

  // Other names for the same wires on the sheet: ADD[7:0] = ADD_out; ADL[7:0] = ADL_in; Cin = C_in; ACC_SB = Ctrl[0];
  //   DB_ACC = Ctrl[1]; ACC_DB = Ctrl[2]; SP_SB = Ctrl[3]; SP_DB = Ctrl[4]; SB_X = Ctrl[5]; X_SB = Ctrl[6];
  //   SB_Y = Ctrl[7]; Y_SB = Ctrl[8]; ADD_SB = Ctrl[9]; DB_A = Ctrl[10]; SB_B = Ctrl[11]; ADL_B = Ctrl[12];
  //   DB_SP = Ctrl[13]; SB_DB = Ctrl[14]; DB_SB = Ctrl[15]; ALU_Ctrl[2:0] = Ctrl[18:16]; DB_OUT = Ctrl[19];
  //   P[14:0] = {Ctrl_P, Ctrl[30:20]}; IR_5 = IR5; SB[7:0] = SB_out; SP[7:0] = SP_out
endmodule
