// Digital circuit 3-P.dig as structural Verilog
module _3_P (
  input  IR5,
  input  [7:0] DB_in,
  input  [14:0] Ctrl,
  input  ACR,
  input  AVR,
  input  Clock,
  output [7:0] DB_out
);

  wire C, C_q, DBZ, driver_2_out, driver_5_out, driver_7_out, driver_11_out, N, N_q, or_1_out, or_2_out,
       or_3_out, V, V_q, Z, Z_q;

  nor nor_1 (DBZ, DB_in[7], DB_in[6], DB_in[5], DB_in[4], DB_in[3], DB_in[2], DB_in[1], DB_in[0]);
  assign DB_out = Ctrl[0] ? {N, V, 4'b0000, Z, C} : 8'bz;  // Driver driver_1
  PullDown #(.Bits(8)) pulldown_1 (.out(DB_out));
  assign driver_2_out = Ctrl[1] ? DB_in[0] : 1'bz;  // Driver driver_2
  assign driver_2_out = Ctrl[2] ? IR5 : 1'bz;  // Driver driver_3
  assign driver_2_out = Ctrl[3] ? ACR : 1'bz;  // Driver driver_4
  or or_1 (or_1_out, Ctrl[1], Ctrl[2], Ctrl[3]);
  assign driver_5_out = Ctrl[4] ? DB_in[1] : 1'bz;  // Driver driver_5
  assign driver_5_out = Ctrl[5] ? DBZ : 1'bz;  // Driver driver_6
  or or_2 (or_2_out, Ctrl[4], Ctrl[5]);
  assign driver_7_out = Ctrl[6] ? DB_in[6] : 1'bz;  // Driver driver_7
  assign driver_7_out = Ctrl[7] ? AVR : 1'bz;  // Driver driver_8
  assign driver_7_out = Ctrl[8] ? 1'b1 : 1'bz;  // Driver driver_9
  assign driver_7_out = Ctrl[9] ? 1'b0 : 1'bz;  // Driver driver_10
  or or_3 (or_3_out, Ctrl[6], Ctrl[7], Ctrl[8], Ctrl[9]);
  assign driver_11_out = Ctrl[10] ? DB_in[7] : 1'bz;  // Driver driver_11
  Register u_C (.D(driver_2_out), .C(Clock), .en(or_1_out), .Q(C_q));
  Register u_Z (.D(driver_5_out), .C(Clock), .en(or_2_out), .Q(Z_q));
  Register u_V (.D(driver_7_out), .C(Clock), .en(or_3_out), .Q(V_q));
  Register u_N (.D(driver_11_out), .C(Clock), .en(Ctrl[10]), .Q(N_q));
  assign C = Ctrl[11] ? C_q : 1'bz;  // Driver driver_12
  assign Z = Ctrl[12] ? Z_q : 1'bz;  // Driver driver_13
  assign V = Ctrl[13] ? V_q : 1'bz;  // Driver driver_14
  assign N = Ctrl[14] ? N_q : 1'bz;  // Driver driver_15

  // Other names for the same wires on the sheet: P_DB = Ctrl[0]; DB0_C = Ctrl[1]; IR5_C = Ctrl[2]; ACR_C = Ctrl[3];
  //   DB1_Z = Ctrl[4]; DBZ_Z = Ctrl[5]; DB6_V = Ctrl[6]; AVR_V = Ctrl[7]; _1_V = Ctrl[8]; _0_V = Ctrl[9];
  //   DB7_N = Ctrl[10]; C_DB = Ctrl[11]; Z_DB = Ctrl[12]; V_DB = Ctrl[13]; N_DB = Ctrl[14]; DB0 = DB_in[0];
  //   DB1 = DB_in[1]; DB6 = DB_in[6]; DB7 = DB_in[7]
endmodule
