// Digital circuit 4-INF.dig as structural Verilog
module _4_INF (
  input  Clock,
  input  IR5,
  input  C_in,
  input  [51:0] Ctrl,
  input  [7:0] IDL_in,
  output [7:0] Out,
  output [7:0] ABL,
  output [7:0] ABH
);

  wire [7:0] ADD, ADH, ADL, DB__PC, SB, SP;

  assign ABH = Ctrl[42] ? ADH : 8'bz;  // Driver driver_1
  assign ABL = Ctrl[43] ? ADL : 8'bz;  // Driver driver_2
  assign DB__PC = Ctrl[44] ? IDL_in : 8'bz;  // Driver driver_3
  _5_PC _5_pc_1 (
    .ADL_in(ADL), .ADH_in(ADH), .SB(SB), .Ctrl_PC({Ctrl[47], Ctrl[38:31]}), .Clock(Clock), .ADL_out(ADL),
    .ADH_out(ADH), .DB(DB__PC));
  PullDown #(.Bits(8)) pulldown_1 (.out(DB__PC));
  _2_BUS _2_bus_1 (
    .Clock(Clock), .DB_in(DB__PC), .Ctrl(Ctrl[30:0]), .IR5(IR5), .C_in(C_in), .Ctrl_P(Ctrl[51:48]),
    .SP_out(SP), .SB_out(SB), .ADD_out(ADD), .Out(Out), .ADL_in(ADL));
  assign ADL = Ctrl[39] ? SP : 8'bz;  // Driver driver_4
  assign ADL = Ctrl[40] ? ADD : 8'bz;  // Driver driver_5
  assign ADL = Ctrl[45] ? IDL_in : 8'bz;  // Driver driver_6
  assign ADH = Ctrl[41] ? SB : 8'bz;  // Driver driver_7
  assign ADH = Ctrl[46] ? IDL_in : 8'bz;  // Driver driver_8

  // Other names for the same wires on the sheet: Ctrl_bus[30:0] = Ctrl[30:0]; Ctrl_PC_0_7[7:0] = Ctrl[38:31];
  //   SP_ADL = Ctrl[39]; ADD_ADL = Ctrl[40]; SB_ADH = Ctrl[41]; ADH_ABH = Ctrl[42]; ADL_ABL = Ctrl[43];
  //   IDL_DB = Ctrl[44]; IDL_ADL = Ctrl[45]; IDL_ADH = Ctrl[46]; Ctrl_PC_8 = Ctrl[47]; Ctrl_P[3:0] = Ctrl[51:48];
  //   IDL[7:0] = IDL_in
endmodule
