// Digital circuit 5-PC.dig as structural Verilog
module _5_PC (
  input  [7:0] ADL_in,
  input  [7:0] ADH_in,
  input  [7:0] SB,
  input  [8:0] Ctrl_PC,
  input  Clock,
  output [7:0] ADL_out,
  output [7:0] ADH_out,
  output [7:0] DB
);

  wire or_1_out, or_2_out;
  wire [7:0] driver_1_out, driver_6_out, PCH_inc, PCH_q, PCL_inc, PCL_q;

  or or_1 (or_1_out, Ctrl_PC[0], Ctrl_PC[8], Ctrl_PC[2]);
  assign driver_1_out = Ctrl_PC[0] ? ADL_in : 8'bz;  // Driver driver_1
  assign driver_1_out = Ctrl_PC[8] ? SB : 8'bz;  // Driver driver_2
  assign driver_1_out = Ctrl_PC[2] ? PCL_inc : 8'bz;  // Driver driver_3
  Register #(.Bits(8)) PCL (.D(driver_1_out), .C(Clock), .en(or_1_out), .Q(PCL_q));
  assign DB = Ctrl_PC[4] ? PCL_q : 8'bz;  // Driver driver_4
  assign ADL_out = Ctrl_PC[6] ? PCL_q : 8'bz;  // Driver driver_5
  or or_2 (or_2_out, Ctrl_PC[1], Ctrl_PC[3]);
  PC_INC pc_inc_1 (.PCH_in(PCH_q), .PCL_in(PCL_q), .PCH_out(PCH_inc), .PCL_out(PCL_inc));
  assign driver_6_out = Ctrl_PC[1] ? ADH_in : 8'bz;  // Driver driver_6
  assign driver_6_out = Ctrl_PC[3] ? PCH_inc : 8'bz;  // Driver driver_7
  Register #(.Bits(8)) PCH (.D(driver_6_out), .C(Clock), .en(or_2_out), .Q(PCH_q));
  assign DB = Ctrl_PC[5] ? PCH_q : 8'bz;  // Driver driver_8
  assign ADH_out = Ctrl_PC[7] ? PCH_q : 8'bz;  // Driver driver_9

  // Other names for the same wires on the sheet: ADL_PCL = Ctrl_PC[0]; ADH_PCH = Ctrl_PC[1]; PCL_PCL = Ctrl_PC[2];
  //   PCH_PCH = Ctrl_PC[3]; PCL_DB = Ctrl_PC[4]; PCH_DB = Ctrl_PC[5]; PCL_ADL = Ctrl_PC[6]; PCH_ADH = Ctrl_PC[7];
  //   SB_PCL = Ctrl_PC[8]
endmodule
