// Digital circuit 6-INT.dig as structural Verilog
module _6_INT (
  input  clk
);

  wire _0_IPC, ADRCTRL, C_in, D_HRH, D_HRL, D_IDL, H_PROM, IPC_ALT, IPC_IPC, IPC_Sel, IPCCTRL, IR5, ITRCTRL,
       LDRAM, nand_1_out, not_1_out, PROM_AROM_Disable, PROMCTRL;
  wire [3:0] _4_inf_1_out, _4_inf_1_out_2;
  wire [7:0] ABL, add_1_s, Addressing_d, D, driver_1_out, driver_2_out, IDL, ipc_1_out, multiplexer_1_out,
       multiplexer_2_out, or_1_out, register_1_q, register_1_q_2, register_2_q, register_2_q_2;
  wire [10:0] Instruction_2_d;
  wire [15:0] IR_q;
  wire [15:8] _4_inf_1_abh;
  wire [51:0] Ctrl_inf;
  wire [63:0] Instruction_d;

  assign or_1_out = IDL | driver_1_out;  // Or or_1, 8 bits wide
  assign driver_1_out = D_IDL ? D : 8'bz;  // Driver driver_1
  PullDown #(.Bits(8)) pulldown_1 (.out(driver_1_out));
  nand nand_1 (nand_1_out, clk, PROM_AROM_Disable);
  Register #(.Bits(16)) register_1 (.D({ABL, D}), .C(nand_1_out), .en(1'b1), .Q({register_1_q_2, register_1_q}));
  _4_INF _4_inf_1 (
    .Clock(clk), .C_in(C_in), .IDL_in(or_1_out), .Ctrl(Ctrl_inf), .IR5(IR5), .ABH(_4_inf_1_abh), .ABL(ABL),
    .Out({_4_inf_1_out_2, _4_inf_1_out}));
  Multiplexer #(.Bits(8)) multiplexer_1 (
    .sel(ADRCTRL), .in_0(register_1_q), .in_1(register_1_q_2), .out(multiplexer_1_out));
  PullDown pulldown_2 (.out(ADRCTRL));
  RAMDualPort #(.AddrBits(16), .Bits(8)) ramdualport_1 (
    .A(IR_q), .Din(driver_2_out), .str(LDRAM), .C(clk), .ld(1'b1), .D(D));
  ROM #(.AddrBits(8), .Bits(8)) Addressing (.A(multiplexer_1_out), .sel(1'b1), .D(Addressing_d));
  assign driver_2_out = LDRAM ? IR_q[15:8] : 8'bz;  // Driver driver_2
  PullDown #(.Bits(16)) pulldown_3 (.out({_4_inf_1_abh, ABL}));
  IPC ipc_1 (.In(ABL), .Ctrl({IPC_IPC, IPC_Sel, IPC_ALT, _0_IPC, clk, IPCCTRL}), .Out(ipc_1_out));
  Register #(.Bits(16)) IR (.D({_4_inf_1_abh, ABL}), .C(clk), .en(PROMCTRL), .Q(IR_q));
  Seven_Seg_Hex seven_seg_hex_1 (.d(_4_inf_1_out_2), .dp(1'b0));
  Seven_Seg_Hex seven_seg_hex_2 (.d(_4_inf_1_out), .dp(1'b0));
  Add #(.Bits(8)) add_1 (.a(register_2_q), .b(ipc_1_out), .c_i(1'b0), .s(add_1_s));  // open: c_o
  BitSelector #(.Selector_Bits(4)) bitselector_1 (.in(IR_q), .sel(4'b0101), .out(IR5));
  Register #(.Bits(16)) register_2 (
    .D({add_1_s, Addressing_d}), .C(clk), .en(1'b1), .Q({register_2_q_2, register_2_q}));
  Multiplexer #(.Bits(8)) multiplexer_2 (
    .sel(ITRCTRL), .in_0(register_2_q), .in_1(register_2_q_2), .out(multiplexer_2_out));
  PullDown pulldown_4 (.out(ITRCTRL));
  ROM #(.AddrBits(8), .Bits(64)) Instruction (.A(multiplexer_2_out), .sel(1'b1), .D(Instruction_d));
  ROM #(.AddrBits(8), .Bits(11)) Instruction_2 (.A(multiplexer_2_out), .sel(1'b1), .D(Instruction_2_d));
  not not_1 (not_1_out, clk);
  Register #(.Bits(64)) register_3 (
    .D(Instruction_d), .C(not_1_out), .en(1'b1),
    .Q({IDL[6:0], _0_IPC, IPC_IPC, IPCCTRL, IPC_Sel, PROMCTRL, Ctrl_inf}));
  Register #(.Bits(11)) register_4 (
    .D(Instruction_2_d), .C(not_1_out), .en(1'b1),
    .Q({H_PROM, D_HRH, D_HRL, IPC_ALT, D_IDL, ADRCTRL, ITRCTRL, PROM_AROM_Disable, LDRAM, C_in, IDL[7]}));

  // Other names for the same wires on the sheet: Clock = clk
endmodule
