// Digital circuit INSTR FORM.dig as structural Verilog
module INSTR_FORM (
  input  [7:0] IPC_in,
  input  [7:0] PC_in,
  output [7:0] Out
);

  wire [0:0] not_1_out;
  wire [3:0] add_1_s, mul_1_mul, sub_1_s;
  wire [7:0] add_2_s, mul_2_mul;

  not not_1 (not_1_out[0], PC_in[0]);
  Mul #(.Bits(2)) mul_1 (.a({1'b0, not_1_out[0]}), .b(2'b10), .mul(mul_1_mul));
  Add #(.Bits(4)) add_1 (.a(mul_1_mul), .b({3'b000, PC_in[0]}), .c_i(1'b0), .s(add_1_s));  // open: c_o
  Sub #(.Bits(4)) sub_1 (.a(add_1_s), .b(4'b0001), .c_i(1'b0), .s(sub_1_s));  // open: c_o
  Mul #(.Bits(4)) mul_2 (.a(sub_1_s), .b(4'b0010), .mul(mul_2_mul));
  Add #(.Bits(8)) add_2 (.a({4'b0000, add_1_s}), .b(mul_2_mul), .c_i(1'b0), .s(add_2_s));  // open: c_o
  Add #(.Bits(8)) add_3 (.a(IPC_in), .b(add_2_s), .c_i(1'b0), .s(Out));  // open: c_o
endmodule
