// Digital circuit IPC.dig as structural Verilog
module IPC (
  input  [5:0] Ctrl,
  input  [7:0] In,
  output [7:0] Out
);

  wire [7:0] add_1_s, driver_1_out, instr_form_1_out, IPC, multiplexer_1_out;

  Multiplexer #(.Bits(8)) multiplexer_1 (.sel(Ctrl[4]), .in_0(8'h1), .in_1(In), .out(multiplexer_1_out));
  Add #(.Bits(8)) add_1 (.a(IPC), .b(multiplexer_1_out), .c_i(1'b0), .s(add_1_s));  // open: c_o
  INSTR_FORM instr_form_1 (.IPC_in(multiplexer_1_out), .PC_in(IPC), .Out(instr_form_1_out));
  assign driver_1_out = Ctrl[5] ? add_1_s : 8'bz;  // Driver driver_1
  assign driver_1_out = Ctrl[2] ? {8{1'b0}} : 8'bz;  // Driver driver_2
  assign driver_1_out = Ctrl[3] ? instr_form_1_out : 8'bz;  // Driver driver_3
  Register #(.Bits(8), .isProgramCounter("true")) u_IPC (.D(driver_1_out), .C(Ctrl[1]), .en(1'b1), .Q(IPC));
  assign Out = Ctrl[0] ? IPC : 8'bz;  // Driver driver_4

  // Other names for the same wires on the sheet: IPCCTRL = Ctrl[0]; Clock = Ctrl[1]; _0_IPC = Ctrl[2];
  //   IPC_ALT = Ctrl[3]; IPC_Sel = Ctrl[4]; IPC_IPC = Ctrl[5]
endmodule
