// Digital circuit OVER.dig as structural Verilog
module OVER (
  input  Overflow,
  input  [7:0] A,
  input  [7:0] B,
  output FLAG
);

  wire xnor_1_out, xor_1_out;

  xor xor_1 (xor_1_out, Overflow, A[7]);
  xnor xnor_1 (xnor_1_out, A[7], B[7]);
  and and_1 (FLAG, xor_1_out, xnor_1_out);
endmodule
