// Digital circuit PC INC.dig as structural Verilog
module PC_INC (
  input  [7:0] PCH_in,
  input  [7:0] PCL_in,
  output [7:0] PCH_out,
  output [7:0] PCL_out
);

  Add #(.Bits(16)) add_1 (.a({PCH_in, PCL_in}), .b(16'h1), .c_i(1'b0), .s({PCH_out, PCL_out}));  // open: c_o
endmodule
