// Digital circuit SUM.dig as structural Verilog
module SUM (
  input  Cin,
  input  [7:0] A,
  input  [7:0] B,
  output Cout,
  output [7:0] SUM
);

  wire add_2_c_o, add_3_c_o, add_4_c_o, add_5_c_o, add_6_c_o, add_7_c_o, add_8_c_o;

  Add add_1 (.a(B[7]), .b(A[7]), .c_i(add_2_c_o), .s(SUM[7]), .c_o(Cout));
  Add add_2 (.a(B[6]), .b(A[6]), .c_i(add_3_c_o), .s(SUM[6]), .c_o(add_2_c_o));
  Add add_3 (.a(B[5]), .b(A[5]), .c_i(add_4_c_o), .s(SUM[5]), .c_o(add_3_c_o));
  Add add_4 (.a(B[4]), .b(A[4]), .c_i(add_5_c_o), .s(SUM[4]), .c_o(add_4_c_o));
  Add add_5 (.a(B[3]), .b(A[3]), .c_i(add_6_c_o), .s(SUM[3]), .c_o(add_5_c_o));
  Add add_6 (.a(B[2]), .b(A[2]), .c_i(add_7_c_o), .s(SUM[2]), .c_o(add_6_c_o));
  Add add_7 (.a(B[1]), .b(A[1]), .c_i(add_8_c_o), .s(SUM[1]), .c_o(add_7_c_o));
  Add add_8 (.a(B[0]), .b(A[0]), .c_i(Cin), .s(SUM[0]), .c_o(add_8_c_o));
  // Pins of 1 and 8 bits meet at SUM
endmodule
